# Fritzing sketch 12v-easyDriver (saved by Fritzing 0.9.1b)

parts:
  Part1 = Arduino Uno (Rev3)
  Part2 = EasyDriver_v44
  M1 = Stepper Motor - Bipolar  # not connected

nets:
  GND: Part1.GND, Part2.GND
  N1: Part1.D2, Part2.DIR
  N2: Part1.D3_PWM, Part2.STEP
  N3: Part1.VIN, Part2.V+

notes:
  Plug a 12V 1A DC power supply into the Arduino.
  Don't go over 12V with this setup!
